# Fritzing sketch hitachi_display_i2c (saved by Fritzing 0.7.11b)
stripboards: 1

parts:
  U2 = atmega168 [package=dip]
  LCD1 = LCD screen
  R1 = Trimmer Potentiometer [maximum_resistance=10kΩ package=THT]
  J2 = male pin header, 6 pins [form="♂ (male)"]
  J3 = male pin header, 3 pins [form="♂ (male)"]
  J4 = male pin header, 3 pins [form="♂ (male)"]  # not connected
  LED1 = LED - 5mm [color="Red (633nm)" package="5 mm [THT]"]
  C1 = Ceramic Capacitor [capacitance=10pF package="100 mil [THT, multilayer]"]
  XTAL1 = CRYSTAL - kHz [frequency="16 Mhz"]
  C2 = Ceramic Capacitor [capacitance=10pF package="100 mil [THT, multilayer]"]

nets:
  N1: U2.RESET, J3.pin1
  N2: U2.D0_(RX), J2.pin6
  N3: U2.D1_(TX), J2.pin5
  N4: U2.D2, LCD1.DB7
  N5: U2.D3_(PWM), LCD1.DB6
  N6: U2.D4, LCD1.DB5
  VCC: U2.VCC, LCD1.VDD, LCD1.DB1, LCD1.LED+, R1.leg1
  N7: U2.GND#7, LCD1.VSS, LCD1.R/W, LCD1.DB3, LCD1.LED-, R1.leg2, LED1.cathode, C1.0, C2.0
  N8: U2.XLAT1, C1.1, XTAL1.pin_0
  N9: U2.XLAT2, XTAL1.pin_1, C2.1
  N10: U2.D5_(PWM), LCD1.DB0, LCD1.DB4
  N11: U2.D7, LCD1.E
  N12: U2.D8, LCD1.RS
  N13: U2.D9_(PWM), LED1.anode
  N14: U2.D12, J3.pin3
  N15: U2.D13, J3.pin2
  N16: U2.AVCC, J2.pin4
  N17: U2.GND#21, J2.pin3
  N18: U2.A4, J2.pin1
  N19: U2.A5, J2.pin2
  N20: LCD1.V0, LCD1.DB2, R1.wiper
