# Fritzing sketch nokia_display_and_nfc_i2c (saved by Fritzing 0.8.7b)
stripboards: 1

parts:
  J1 = female pin header, 8 pins [form="♀ (female)"]
  Y1 = Resonator [frequency="16 Mhz" package=THT]  # not connected
  J2 = male pin header, 4 pins [form="♂ (male)"]
  J3 = female pin header, 8 pins [form="♀ (female)"]
  LED1 = RGB LED (com. anode, rbg) [package="5 mm [THT]"]
  U2 = atmega328 [package=dip]

nets:
  N1: J1.pin1, J1.pin2, J1.pin3, J1.pin4, J1.pin5, J1.pin6, J1.pin7, J1.pin8, J2.pin1, J2.pin2, J2.pin3, J2.pin4, J3.pin1, J3.pin2, J3.pin7, J3.pin8, LED1.common_anode, U2.D2, U2.GND, U2.D7, U2.D8, U2.D9_(PWM), U2.D11_(PWM), U2.D13, U2.AVCC, U2.A4
  N2: J3.pin3, U2.A0
  N3: J3.pin4, U2.A1
  N4: J3.pin5, U2.A2
  N5: J3.pin6, U2.A3
  N6: LED1.red_cathode, U2.D3_(PWM)
  N7: LED1.blue_cathode, U2.D5_(PWM)
  N8: LED1.green_cathode, U2.D6_(PWM)

notes:
  Nokia Display
