# Fritzing sketch nokia_display_i2c (saved by Fritzing 0.7.11b)
stripboards: 1

parts:
  U2 = atmega168 [package=dip]
  J1 = female pin header, 8 pins [form="♀ (female)"]
  Y1 = Resonator [frequency="16 Mhz" package=THT]  # not connected
  J2 = male pin header, 7 pins [form="♂ (male)"]
  J4 = shrouded pin header, 6 pins [form="♂ (shrouded male)"]
  GLCD_128x1 = 128 x 64 Graphic LCD  # not connected

nets:
  N1: U2.RESET, U2.GND#21, J1.pin8, J2.pin4, J4.pin1
  N2: U2.D0_(RX), J2.pin1, J2.pin6
  N3: U2.D1_(TX), J2.pin7
  N4: U2.D7, J1.pin2
  N5: U2.D8, J1.pin1
  N6: U2.D9_(PWM), J1.pin3, J4.pin4
  N7: U2.D11_(PWM), J1.pin4, J4.pin2
  N8: U2.D13, J1.pin5, J4.pin5
  N9: U2.AVCC, J1.pin6, J2.pin5, J4.pin3
  N10: U2.AREF, J1.pin7
  N11: U2.A4, J2.pin2
  N12: U2.A5, J2.pin3
